# Fritzing sketch moisture detection sketch (saved by Fritzing 0.9.3b)
breadboards: 1

parts:
  Part1 = Soil Moisture Sensor
  YL-83_-_Control_Board1 = YL-83 Rain Sensor - Control Board
  Raspberry_Pi_1 = Raspberry Pi 3 [part_number=RPI-3-V1.2]
  LED1 = smd LED [color="Red (633nm)" package="0805 [SMD]"]
  R1 = Resistor [tolerance=±5% resistance=220 package="0805 [SMD]"]

nets:
  N1: Part1.GND, YL-83_-_Control_Board1.NEG
  N2: Part1.VCC, YL-83_-_Control_Board1.POS
  VCC: YL-83_-_Control_Board1.VCC, Raspberry_Pi_1.3v3
  GND: YL-83_-_Control_Board1.GND, Raspberry_Pi_1.GND, R1.Pin_1
  N3: YL-83_-_Control_Board1.DO, Raspberry_Pi_1.GIPO21
  N4: Raspberry_Pi_1.GIPO18, LED1.anode
  N5: LED1.cathode, R1.Pin_0

notes:
  GPIO PIN 1
  VCC = 3.3v
  GPIO Pin 21
  3.3v tolerant
  LED turns ON when water is detected
  Here we have a moisture sensor that is connected to a control board that is using a raspberry pi 3 for power and configurations. Using pin 1 for 3.3v of pwr and pin 21 for configurations using a Python script. The Python script has one function and it prints a string to notify that water has been detected along with lighting up an LED light bulb. The scipt is in an infinite loop repeating every 1 second and runs at startup of the raspberry pi.
  GPIO PIN 6
  GND
  GPIO Pin 12
  3.3v tolerant

custom parts:
  YL-83 Rain Sensor - Control Board: The YL-83 is a rain sensor that has more resistance when dry and less resistance when wet. The module runs at 5V.
